# Fritzing sketch Fritzing File (saved by Fritzing 0.9.3b)
breadboards: 1

parts:
  Part1 = Arduino Uno (Rev3)
  Bauteil4 = Barometric Pressure Sensor - BMP085 Breakout
  GY2 = MPU-6050 Board GY-521 [form="♀ (female)" package=THT]
  Part2 = MicroSD Card Module
  J1 = Basic Servo
  J2 = Basic Servo

nets:
  N1: Part1.A4/SDA, Bauteil4.SDA, GY2.pin4
  N2: Part1.A5/SCL, Bauteil4.SCL, GY2.pin3
  N3: Part1.D11_PWM/MOSI, Part2.MOSI
  N4: Part1.D12/MISO, Part2.MISO
  N5: Part1.D13/SCK, Part2.SCK
  GND: Part1.GND, Bauteil4.GND, GY2.pin2, Part2.GND, J1.gnd, J2.gnd
  N6: Part1.D2, J1.pulse
  N7: Part1.D3_PWM, J2.pulse
  N8: Part1.D4, Part2.CS
  VCC: Part1.5V, Bauteil4.VCC, GY2.pin1, Part2.VCC, J1.vcc, J2.vcc

notes:
  MPU6050
  RED --> 5V
  BLACK --> GND
  PURPLE --> SCK -->A5
  GREEN --> SDA -->A4
  BMP180
  RED --> 5V
  BLACK --> GND
  PURPLE --> SCK -->A5
  GREEN --> SDA -->A4
  SD CARD MODULE
  RED --> 5V
  BLACK --> GND
  YELLOW --> MISO --> D12
  GREY --> MOSI --> D11
  ORENGE --> SCK --> D13
  BLUE --> CS --> D4

custom parts:
  MPU-6050 Board GY-521: Acelerometro y Giroscopio MPU-6050 Board GY-521
